# Fritzing sketch circuitoAMST (saved by Fritzing 0.8.7b)

parts:
  Part3 = HX711 Weighing Sensor Module
  Load_Cell2 = Load Cell - Red/white/black/green
  Part4 = Arduino Ethernet Shield (Rev3)
  VCC1 = Battery block 9V
  Part1 = Arduino Uno (Rev3)

nets:
  VCC: Part3.VCC, Part1.VIN
  GND: Part3.GND, Part4.GND, VCC1.-, Part1.GND
  N1: Part3.DO/RX, Part1.A2
  N2: Part3.CK/TX, Part1.A3
  N3: Part3.E+, Load_Cell2.wire1
  N4: Part3.E-, Load_Cell2.wire2
  N5: Part3.A+, Load_Cell2.wire3
  N6: Part3.A-, Load_Cell2.wire4
  5V: Part4.5V, VCC1.+, Part1.5V
  N7: Part4.D8, Part1.D8
  N8: Part4.PWM_D9, Part1.D9_PWM
  N9: Part4.ETH_CS, Part1.D10_PWM/SS
  N10: Part4.PWM_D11, Part1.D11_PWM/MOSI
  N11: Part4.SPI/D13, Part1.D13/SCK
  N12: Part4.RX/D0, Part1.D0/RX
  N13: Part4.TX/D1, Part1.D1/TX
  N14: Part4.PWM_D6, Part1.D6_PWM
  N15: Part4.D7, Part1.D7

custom parts:
  Load Cell - Red/white/black/green: A rectangle load cell/weighting pressure Sensor with four wires - Red, white, black, green. Normally corresponding with E+, E-, A+, A- respectively.
